// Logisim project Control Unit.circ as structural Verilog: 4 circuits, main circuit main
module main (
  input  in_1,
  input  in_2,
  input  in_3,
  input  in_4,
  input  [5:0] in_5,
  input  [5:0] in_6,
  input  [3:0] in_7,
  input  [3:0] in_8,
  output IorD,
  output [3:0] out_10,
  output [1:0] RegDst,
  output [2:0] Branch_Control,
  output [2:0] ALU_SrcB,
  output [2:0] MemtoReg,
  output Dir_A,
  output Dir_B,
  output HI_LO_Write,
  output Load_A_B,
  output Load_ALU_HI,
  output RegWrite,
  output out_21,
  output DataWrite,
  output MemWrite,
  output tty_EN,
  output kbd_EN
);

  wire CS, d_ff_1_q, d_ff_2_q, d_ff_3_q, d_ff_21_q, demultiplexer_1_out0, demultiplexer_2_out0,
       demultiplexer_2_out1, demultiplexer_3_out3, demultiplexer_4_out0, demultiplexer_4_out1,
       demultiplexer_5_out1, demultiplexer_6_out0, END_q, IDLE_q, nor_1_out, or_1_out, or_2_out, or_3_out,
       or_4_out, or_5_out, or_6_out, or_7_out, undriven, undriven_2, wait_Ram;
  wire [2:0] Op_sel;
  wire [3:0] counter_1_q, RT__WT;

  D_Flip_Flop IDLE (.clk(in_3), .D(demultiplexer_1_out0), .Q(IDLE_q), .preset(or_1_out));  // open: Qn, en, reset
  or or_1 (or_1_out, in_1, ~in_4);  // OR_Gate
  Multiplexer #(.width(4), .enable("false")) multiplexer_1 (.in0(in_7), .in1(in_8), .out(RT__WT), .sel(in_2));
  or or_2 (or_2_out, IDLE_q, undriven);
  Demultiplexer #(.enable("false")) demultiplexer_1 (.out0(demultiplexer_1_out0), .out1(CS), .in(or_2_out), .sel(in_4));
  or or_3 (or_3_out, demultiplexer_2_out0, CS);
  // Probe on Op_sel
  CU_Op_Decoder cu_op_decoder_1 (.in_1(in_5), .Op_CU(Op_sel), .in_2(in_6));
  // Probe on out_10
  ALU_Decoder alu_decoder_1 (.in_1(in_5), .in_2(in_6), .out_3(out_10));
  Branch_Control_Decoder branch_control_decoder_1 (.in_1(in_5), .in_2(in_6), .Branch_Control(Branch_Control));
  Counter #(.width(4), .max('hf)) counter_1 (
    .load(CS), .D(RT__WT), .count(d_ff_1_q), .Q(counter_1_q), .clk(in_3));  // open: carry, clr
  D_Flip_Flop d_ff_1 (.clk(in_3), .D(CS), .Q(d_ff_1_q), .reset(in_1));  // open: Qn, preset, en
  D_Flip_Flop d_ff_2 (.clk(in_3), .D(or_3_out), .Q(d_ff_2_q), .reset(in_1));  // open: Qn, preset, en
  Demultiplexer #(.enable("false")) demultiplexer_2 (
    .out0(demultiplexer_2_out0), .out1(demultiplexer_2_out1), .in(d_ff_2_q), .sel(wait_Ram));
  // Probe on Branch_Control
  nor nor_1 (nor_1_out, counter_1_q[0], counter_1_q[1], counter_1_q[2], counter_1_q[3]);
  D_Flip_Flop d_ff_3 (.clk(in_3), .D(demultiplexer_2_out1), .Q(d_ff_3_q), .reset(in_1));  // open: Qn, preset, en
  and and_1 (wait_Ram, nor_1_out, d_ff_1_q);
  Demultiplexer #(.select(3), .enable("false")) demultiplexer_3 (
    .out1(Load_A_B), .out2(Load_A_B), .out3(demultiplexer_3_out3), .in(d_ff_3_q), .sel(Op_sel));  // open: out0, out4, out5, out6, out7
  D_Flip_Flop d_ff_4 (.clk(in_3), .reset(in_1));  // open: D, Q, Qn, preset, en
  D_Flip_Flop d_ff_5 (.clk(in_3), .reset(in_1));  // open: D, Q, Qn, preset, en
  D_Flip_Flop d_ff_6 (.clk(in_3), .D(Load_A_B), .Q(ALU_SrcB[0]), .reset(in_1));  // open: Qn, preset, en
  D_Flip_Flop d_ff_7 (.clk(in_3), .D(Load_A_B), .Q(ALU_SrcB[0]), .reset(in_1));  // open: Qn, preset, en
  D_Flip_Flop d_ff_8 (.clk(in_3), .D(Load_A_B), .Q(ALU_SrcB[0]), .reset(in_1));  // open: Qn, preset, en
  D_Flip_Flop d_ff_9 (.clk(in_3), .reset(in_1));  // open: D, Q, Qn, preset, en
  D_Flip_Flop d_ff_10 (.clk(in_3), .reset(in_1));  // open: D, Q, Qn, preset, en
  D_Flip_Flop d_ff_11 (.clk(in_3), .reset(in_1));  // open: D, Q, Qn, preset, en
  D_Flip_Flop d_ff_12 (.clk(in_3), .reset(in_1));  // open: D, Q, Qn, preset, en
  D_Flip_Flop d_ff_13 (.clk(in_3), .reset(in_1));  // open: D, Q, Qn, preset, en
  D_Flip_Flop d_ff_14 (.clk(in_3), .reset(in_1));  // open: D, Q, Qn, preset, en
  D_Flip_Flop d_ff_15 (.clk(in_3), .reset(in_1));  // open: D, Q, Qn, preset, en
  // D_Flip_Flop d_ff_16: pin names not known; wires that end beside it: ALU_SrcB[0], in_3, in_1, CS
  D_Flip_Flop d_ff_17 (.clk(in_3), .D(ALU_SrcB[0]), .Q(RegDst[0]), .reset(in_1));  // open: Qn, preset, en
  D_Flip_Flop d_ff_18 (.clk(in_3), .D(ALU_SrcB[0]), .Q(HI_LO_Write), .reset(in_1));  // open: Qn, preset, en
  D_Flip_Flop d_ff_19 (.clk(in_3), .D(undriven_2), .en(undriven_2), .reset(in_1));  // open: Q, Qn, preset
  D_Flip_Flop d_ff_20 (.clk(in_3), .reset(in_1));  // open: D, Q, Qn, preset, en
  Demultiplexer #(.enable("false")) demultiplexer_4 (
    .out0(demultiplexer_4_out0), .out1(demultiplexer_4_out1), .in(d_ff_21_q), .sel(wait_Ram));
  D_Flip_Flop d_ff_21 (.clk(in_3), .D(or_4_out), .Q(d_ff_21_q), .reset(in_1));  // open: Qn, preset, en
  // OR_Gate or_4 has open pins: out=or_4_out
  D_Flip_Flop d_ff_22 (.clk(in_3), .D(ALU_SrcB[0]), .Q(RegDst[0]), .reset(in_1));  // open: Qn, preset, en
  D_Flip_Flop d_ff_23 (.clk(in_3), .reset(in_1));  // open: D, Q, Qn, preset, en
  D_Flip_Flop d_ff_24 (.clk(in_3), .reset(in_1));  // open: D, Q, Qn, preset, en
  D_Flip_Flop d_ff_25 (.clk(in_3), .reset(in_1));  // open: D, Q, Qn, preset, en
  D_Flip_Flop d_ff_26 (.clk(in_3), .reset(in_1));  // open: D, Q, Qn, preset, en
  // D_Flip_Flop d_ff_27: pin names not known; wires that end beside it: RegDst[0], in_3, in_1, IorD
  D_Flip_Flop d_ff_28 (.clk(in_3), .reset(in_1));  // open: D, Q, Qn, preset, en
  // OR_Gate or_5 has open pins: out=or_5_out
  D_Flip_Flop d_ff_29 (.clk(in_3), .reset(in_1));  // open: D, Q, Qn, preset, en
  D_Flip_Flop d_ff_30 (.clk(in_3), .reset(in_1));  // open: D, Q, Qn, preset, en
  Demultiplexer #(.enable("false")) demultiplexer_5 (.out0(CS), .out1(demultiplexer_5_out1));  // open: in, sel
  D_Flip_Flop d_ff_31 (.clk(in_3), .D(or_5_out), .reset(in_1));  // open: Q, Qn, preset, en
  // OR_Gate or_6 has open pins: out=or_6_out
  // OR_Gate or_7 has open pins: out=or_7_out
  D_Flip_Flop d_ff_32 (.clk(in_3), .D(or_6_out), .reset(in_1));  // open: Q, Qn, preset, en
  Demultiplexer #(.enable("false")) demultiplexer_6 (.out0(demultiplexer_6_out0));  // open: out1, in, sel
  D_Flip_Flop d_ff_33 (.clk(in_3), .D(or_7_out), .reset(in_1));  // open: Q, Qn, preset, en
  // Demultiplexer #(.enable("false")) demultiplexer_7: pin names not known; wires that end beside it: wait_Ram, CS
  D_Flip_Flop d_ff_34 (.clk(in_3), .reset(in_1));  // open: D, Q, Qn, preset, en
  D_Flip_Flop d_ff_35 (.clk(in_3), .reset(in_1));  // open: D, Q, Qn, preset, en
  or or_8 (out_21, RegDst[0], HI_LO_Write);
  D_Flip_Flop d_ff_36 (.clk(in_3), .reset(in_1));  // open: D, Q, Qn, preset, en
  D_Flip_Flop END (.clk(in_3), .D(out_21), .Q(END_q), .reset(in_1));  // open: Qn, preset, en

  assign Load_ALU_HI = ALU_SrcB[0];
  assign RegWrite = RegDst[0];

  // Other names for the same wires on the sheet: ALU_Op[3:0] = out_10; ALU_SrcB_0 = ALU_SrcB[0];
  //   ALU_SrcB_1 = ALU_SrcB[1]; ALU_SrcB_2 = ALU_SrcB[2]; Clk = in_3; Func_Code[5:0] = in_6; Op_Code[5:0] = in_5;
  //   PC = out_21; RegDst_t = RegDst[0]; Reset = in_1; RT[3:0] = in_7; RT__WT_RAM_Sel = in_2; start = in_4;
  //   WT[3:0] = in_8

  // Notes on the sheet:
  //   Input Data
  //   pop
  //   push
  //   N * / ALU
  //   Control Unit
  //   hi
  //   lo
  //   * / Alu
  //   inmediatos
  //   halt
  //   rnd
  //   tty
  //   kbd
  //   lw
  //   sw
  //   Output Data
endmodule

module ALU_Decoder (
  input  [5:0] in_1,
  input  [5:0] in_2,
  output [3:0] out_3
);

  wire A_value, add, add_ALU, addi, \and , and_ALU, andi, beq, bgtz, blez, bltz, bne, div, divu, halt, j, jr,
       kbd, lw, Math_op_out, mfhi, mflo, mflo_hi, mult, mulu, nop, \nor , \or , or_ALU, ori, pop, pop_v,
       push, push_pop, push_v, rnd, slt, slt_ALU, slti, sltiu, sltu, sltu_ALU, Special_out, sub, sub_ALU, sw,
       tty, \xor , xor_ALU, xori;

  and Math_op (Math_op_out, ~in_1[0], ~in_1[1], ~in_1[2], ~in_1[3], ~in_1[4], ~in_1[5]);  // AND_Gate
  and pop_push (push_pop, ~in_1[0], ~in_1[1], ~in_1[2], in_1[3], in_1[4], in_1[5]);  // AND_Gate
  and Special (Special_out, in_1[0], in_1[1], in_1[2], in_1[3], in_1[4], in_1[5]);
  and u_add (add, ~in_2[0], ~in_2[1], ~in_2[2], ~in_2[3], ~in_2[4], in_2[5]);  // AND_Gate
  and u_div (div, ~in_2[0], in_2[1], ~in_2[2], in_2[3], in_2[4], ~in_2[5]);  // AND_Gate
  and u_nor (\nor , in_2[0], in_2[1], in_2[2], ~in_2[3], ~in_2[4], in_2[5]);  // AND_Gate
  and u_mfhi (mfhi, ~in_2[0], ~in_2[1], ~in_2[2], ~in_2[3], in_2[4], ~in_2[5]);  // AND_Gate
  and u_halt (halt, in_2[0], in_2[1], in_2[2], in_2[3], in_2[4], in_2[5]);
  and u_Sub (sub, ~in_2[0], in_2[1], ~in_2[2], ~in_2[3], ~in_2[4], in_2[5]);  // AND_Gate
  and u_divu (divu, in_2[0], in_2[1], ~in_2[2], in_2[3], in_2[4], ~in_2[5]);  // AND_Gate
  and u_xor (\xor , ~in_2[0], ~in_2[1], ~in_2[2], in_2[3], ~in_2[4], in_2[5]);  // AND_Gate
  and u_mflo (mflo, ~in_2[0], in_2[1], ~in_2[2], ~in_2[3], in_2[4], ~in_2[5]);  // AND_Gate
  and u_tty (tty, in_2[0], ~in_2[1], ~in_2[2], ~in_2[3], ~in_2[4], ~in_2[5]);  // AND_Gate
  and u_addi (addi, ~in_1[0], ~in_1[1], ~in_1[2], in_1[3], ~in_1[4], ~in_1[5]);  // AND_Gate
  and u_andi (andi, ~in_1[0], ~in_1[1], in_1[2], in_1[3], ~in_1[4], ~in_1[5]);  // AND_Gate
  and u_slti (slti, ~in_1[0], in_1[1], ~in_1[2], in_1[3], ~in_1[4], ~in_1[5]);  // AND_Gate
  and u_beq (beq, ~in_1[0], ~in_1[1], in_1[2], ~in_1[3], ~in_1[4], ~in_1[5]);  // AND_Gate
  and u_bne (bne, in_1[0], ~in_1[1], in_1[2], ~in_1[3], ~in_1[4], ~in_1[5]);  // AND_Gate
  and u_mult (mult, ~in_2[0], ~in_2[1], ~in_2[2], in_2[3], in_2[4], ~in_2[5]);  // AND_Gate
  and u_and (\and , ~in_2[0], ~in_2[1], in_2[2], ~in_2[3], ~in_2[4], in_2[5]);  // AND_Gate
  and u_slt (slt, ~in_2[0], in_2[1], ~in_2[2], in_2[3], ~in_2[4], in_2[5]);  // AND_Gate
  and u_nop (nop, ~in_2[0], ~in_2[1], ~in_2[2], ~in_2[3], ~in_2[4], ~in_2[5]);  // AND_Gate
  and u_rnd (rnd, ~in_2[0], in_2[1], ~in_2[2], ~in_2[3], ~in_2[4], ~in_2[5]);  // AND_Gate
  and u_blez (blez, ~in_1[0], in_1[1], in_1[2], ~in_1[3], ~in_1[4], ~in_1[5]);  // AND_Gate
  and u_bgtz (bgtz, in_1[0], in_1[1], in_1[2], ~in_1[3], ~in_1[4], ~in_1[5]);  // AND_Gate
  and u_bltz (bltz, in_1[0], ~in_1[1], ~in_1[2], ~in_1[3], ~in_1[4], ~in_1[5]);  // AND_Gate
  and u_lw (lw, in_1[0], in_1[1], ~in_1[2], ~in_1[3], ~in_1[4], in_1[5]);  // AND_Gate
  and u_sw (sw, in_1[0], in_1[1], ~in_1[2], in_1[3], ~in_1[4], in_1[5]);  // AND_Gate
  and u_sltiu (sltiu, in_1[0], in_1[1], ~in_1[2], in_1[3], ~in_1[4], ~in_1[5]);  // AND_Gate
  and u_ori (ori, in_1[0], ~in_1[1], in_1[2], in_1[3], ~in_1[4], ~in_1[5]);  // AND_Gate
  and u_xori (xori, ~in_1[0], in_1[1], in_1[2], in_1[3], ~in_1[4], ~in_1[5]);  // AND_Gate
  and u_mulu (mulu, in_2[0], ~in_2[1], ~in_2[2], in_2[3], in_2[4], ~in_2[5]);  // AND_Gate
  and u_or (\or , in_2[0], ~in_2[1], in_2[2], ~in_2[3], ~in_2[4], in_2[5]);  // AND_Gate
  and u_sltu (sltu, in_2[0], in_2[1], ~in_2[2], in_2[3], ~in_2[4], in_2[5]);  // AND_Gate
  and u_jr (jr, ~in_2[0], ~in_2[1], ~in_2[2], in_2[3], ~in_2[4], ~in_2[5]);  // AND_Gate
  and u_kbd (kbd, ~in_2[0], ~in_2[1], in_2[2], ~in_2[3], ~in_2[4], ~in_2[5]);  // AND_Gate
  or or_2 (and_ALU, \and , andi);
  or or_3 (or_ALU, \or , ori);
  or u_mflo_hi (mflo_hi, mflo, mfhi);
  Priority_Encoder #(.select(4)) priority_encoder_1 (
    .in0(mult), .in1(mulu), .in2(div), .in3(divu), .in4(and_ALU), .in5(sub_ALU), .in6(xor_ALU),
    .in7(add_ALU), .in8(or_ALU), .in9(sltu_ALU), .in10(\nor ), .in11(slt_ALU), .in12(mflo_hi),
    .in13(A_value), .out(out_3));  // open: in14, in15, gs, en_out, en_in
  and and_2 (push_v, push_pop, push);
  or or_4 (slt_ALU, slt, slti);
  or or_5 (sltu_ALU, sltu, sltiu);
  or or_6 (xor_ALU, \xor , xori);
  and u_j (j, ~in_1[0], in_1[1], ~in_1[2], ~in_1[3], ~in_1[4], ~in_1[5]);  // AND_Gate
  and u_push (push, in_2[0], ~in_2[1], ~in_2[2], ~in_2[3], ~in_2[4], ~in_2[5]);  // AND_Gate
  and u_pop (pop, ~in_2[0], ~in_2[1], ~in_2[2], ~in_2[3], ~in_2[4], ~in_2[5]);  // AND_Gate
  or or_7 (sub_ALU, beq, sub, bne, push_v);
  and and_3 (pop_v, pop, push_pop);
  or or_8 (A_value, blez, bltz, bgtz);
  or or_9 (add_ALU, lw, add, pop_v, addi, sw);

  // Other names for the same wires on the sheet: ALU_OP_Code[3:0] = out_3; Func_code[5:0] = in_2; Op_Code[5:0] = in_1

  // Notes on the sheet:
  //   Op-Code
  //   Tipo R
  //   Func-Code
  //   Tipo I
  //   Tipo J
endmodule

module Branch_Control_Decoder (
  input  [5:0] in_1,
  input  [5:0] in_2,
  output [2:0] Branch_Control
);

  wire beq, bgtz, blez, bltz, bne, j, jr, nop, Sel;
  wire [2:0] Branch_Control_t;

  and u_nop (nop, ~in_2[0], ~in_2[1], ~in_2[2], ~in_2[3], ~in_2[4], ~in_2[5]);  // AND_Gate
  Priority_Encoder priority_encoder_1 (
    .in0(nop), .in1(beq), .in2(bne), .in3(blez), .in4(bgtz), .in5(bltz), .in6(j), .in7(jr),
    .out(Branch_Control_t), .en_out(Sel));  // open: en_in, gs
  and u_jr (jr, ~in_2[0], ~in_2[1], ~in_2[2], in_2[3], ~in_2[4], ~in_2[5]);  // AND_Gate
  and u_beq (beq, ~in_1[0], ~in_1[1], in_1[2], ~in_1[3], ~in_1[4], ~in_1[5]);  // AND_Gate
  and u_bne (bne, in_1[0], ~in_1[1], in_1[2], ~in_1[3], ~in_1[4], ~in_1[5]);  // AND_Gate
  and u_blez (blez, ~in_1[0], in_1[1], in_1[2], ~in_1[3], ~in_1[4], ~in_1[5]);  // AND_Gate
  and u_bgtz (bgtz, in_1[0], in_1[1], in_1[2], ~in_1[3], ~in_1[4], ~in_1[5]);  // AND_Gate
  and u_bltz (bltz, in_1[0], ~in_1[1], ~in_1[2], ~in_1[3], ~in_1[4], ~in_1[5]);  // AND_Gate
  and u_j (j, ~in_1[0], in_1[1], ~in_1[2], ~in_1[3], ~in_1[4], ~in_1[5]);  // AND_Gate
  Multiplexer #(.width(3), .enable("false")) multiplexer_1 (
    .in0(Branch_Control_t), .in1(3'b000), .out(Branch_Control), .sel(Sel));

  // Other names for the same wires on the sheet: Func_code[5:0] = in_2; Op_Code[5:0] = in_1
endmodule

module CU_Op_Decoder (
  input  [5:0] in_1,
  input  [5:0] in_2,
  output [2:0] Op_CU
);

  wire div, divu, Math, mult, mulu, N, or_1_out, tunnel;

  and Math_op (Math, ~in_1[0], ~in_1[1], ~in_1[2], ~in_1[3], ~in_1[4], ~in_1[5]);  // AND_Gate
  or or_1 (or_1_out, mult, divu, mulu, div);
  and \and  (tunnel, or_1_out, Math);
  and u_N (N, ~tunnel, Math);  // AND_Gate
  and u_divu (divu, in_2[0], in_2[1], ~in_2[2], in_2[3], in_2[4], ~in_2[5]);  // AND_Gate
  and u_div (div, ~in_2[0], in_2[1], ~in_2[2], in_2[3], in_2[4], ~in_2[5]);  // AND_Gate
  and u_mult (mult, ~in_2[0], ~in_2[1], ~in_2[2], in_2[3], in_2[4], ~in_2[5]);  // AND_Gate
  and u_mulu (mulu, in_2[0], ~in_2[1], ~in_2[2], in_2[3], in_2[4], ~in_2[5]);  // AND_Gate
  Priority_Encoder priority_encoder_1 (
    .in1(N), .in2(tunnel), .out(Op_CU));  // open: in0, in3, in4, in5, in6, in7, en_in, gs, en_out

  // Other names for the same wires on the sheet: Func_code[5:0] = in_2; Op_Code[5:0] = in_1

  // Notes on the sheet:
  //   Tipo R
endmodule
