// Logisim project DathaPath.circ as structural Verilog: 2 circuits, main circuit DataPath
module DataPath (
  input  [31:0] in_1,
  input  [31:0] in_2,
  input  [31:0] in_3,
  input  [31:0] in_4,
  input  [3:0] ALU_Op,
  input  [2:0] Branch_Code,
  input  [1:0] ALUSrcB,
  input  [1:0] MemtoReg,
  input  RegDst,
  input  DataWrite,
  input  Load_ALU_HI,
  input  Load_A_and_B,
  input  HI_LO_Write,
  input  RegWrite,
  input  jump,
  input  MemWrite,
  input  PCWrite,
  input  IorD,
  input  IRWrite,
  input  CLK,
  input  RST,
  output [5:0] out_22,
  output [5:0] out_23
);

  wire NF, PC_EN, ZF;
  wire [4:0] Dir_Rd, Dir_Rs, Dir_Rt, multiplexer_3_out;
  wire [15:0] offset;
  wire [25:0] Dir_Salto;
  wire [31:0] A, A_out, ALU_Out, B, B_out, Data_out, HI_O, HI_Out, Instr_q, instruction_data_memory_1_out_5,
       LO_O, multiplexer_1_out, multiplexer_2_out, multiplexer_4_out, offset_ext, PC, PC_prime, ZF_high,
       ZF_result_low;

  Register #(.width(32)) u_PC (.D(PC_prime), .en(PC_EN), .Q(PC), .clk(CLK), .clr(RST));
  Multiplexer #(.width(32), .enable("false")) multiplexer_1 (
    .in0(PC), .in1(ALU_Out), .out(multiplexer_1_out), .sel(IorD));
  Instruction_Data_Memory instruction_data_memory_1 (
    .in_3(multiplexer_1_out), .in_4(B), .out_5(instruction_data_memory_1_out_5), .in_1(CLK), .in_2(MemWrite));
  Register #(.width(32)) Data (
    .D(instruction_data_memory_1_out_5), .en(DataWrite), .Q(Data_out), .clk(CLK));  // open: clr
  Register #(.width(32)) Instr (
    .D(instruction_data_memory_1_out_5), .en(IRWrite), .Q(Instr_q), .clk(CLK));  // open: clr
  or or_1 (PC_EN, PCWrite, jump);
  Instruction_Decoder instruction_decoder_1 (
    .Instruction(Instr_q), .out_2(Dir_Salto), .out_5(Dir_Rd), .out_4(Dir_Rt), .out_3(Dir_Rs), .out_6(offset),
    .out_7(out_22), .out_8(out_23));
  assign offset_ext = {{16{1'b0}}, offset};  // Bit_Extender bit_extender_1
  Branch_Control branch_control_1 (
    .N(NF), .Z(ZF), .j(jump), .PC(PC), .Branch_Code(Branch_Code), .PC_prime(PC_prime),
    .Constant_extended(offset_ext), .Destiny(Dir_Salto), .Register(A));
  Multiplexer #(.select(2), .width(32), .enable("false")) multiplexer_2 (
    .in0(ALU_Out), .in1(Data_out), .in2(LO_O), .in3(HI_O), .out(multiplexer_2_out), .sel(MemtoReg));
  Multiplexer #(.width(5), .enable("false")) multiplexer_3 (
    .in0(Dir_Rt), .in1(Dir_Rd), .out(multiplexer_3_out), .sel(RegDst));
  Register_File_CPU_main main_1 (
    .\Dirección_de_destino (multiplexer_3_out), .R_W(RegWrite), .Datos_de_entrada(multiplexer_2_out),
    .Selector_Salida_A(Dir_Rs), .Selector_Salida_B(Dir_Rt), .Reset(RST), .Clock(CLK), .HI_in(HI_Out),
    .LO_in(ALU_Out), .R_W_HI_LO(HI_LO_Write), .Salida_A(A_out), .Salida_B(B_out), .out_13(HI_O), .out_14(LO_O));
  Register #(.width(32)) u_A (.D(A_out), .en(Load_A_and_B), .Q(A), .clk(CLK));  // open: clr
  Register #(.width(32)) u_B (.D(B_out), .en(Load_A_and_B), .Q(B), .clk(CLK));  // open: clr
  Multiplexer #(.select(2), .width(32), .enable("false")) multiplexer_4 (
    .in0(B), .in2(offset_ext), .out(multiplexer_4_out), .sel(ALUSrcB));  // open: in1, in3
  ALU u_ZF (
    .Input_0(A), .Input_1(multiplexer_4_out), .OpCode(ALU_Op), .Result_Low(ZF_result_low), .High(ZF_high),
    .ZF(ZF), .NF(NF));
  Register #(.width(32)) u_ALU_Out (.D(ZF_result_low), .en(Load_ALU_HI), .Q(ALU_Out), .clk(CLK));  // open: clr
  Register #(.width(32)) u_HI_Out (.D(ZF_high), .en(Load_ALU_HI), .Q(HI_Out), .clk(CLK));  // open: clr

  // Other names for the same wires on the sheet: Func_Code[5:0] = out_23; I0[31:0] = in_1; I1[31:0] = in_3;
  //   I2[31:0] = in_2; I3[31:0] = in_4; Load_A_B = Load_A_and_B; Op_Code[5:0] = out_22
endmodule

module Instruction_Data_Memory (
  input  in_1,
  input  in_2,
  input  [31:0] in_3,
  input  [31:0] in_4,
  output [31:0] out_5
);


  // Other names for the same wires on the sheet: Address[31:0] = in_3; CLK = in_1; RD[31:0] = out_5; WD[31:0] = in_4;
  //   WE = in_2
endmodule
