// Logisim project Instruction Decoder.circ as structural Verilog: 1 circuit, main circuit Instruction Decoder
module Instruction_Decoder (
  input  [31:0] Instruction,
  output [25:0] out_2,
  output [4:0] out_3,
  output [4:0] out_4,
  output [4:0] out_5,
  output [15:0] out_6
);

  wire add_out, addi_out, and_out, andi_out, beq_out, bgtz_out, blez_out, bltz_out, bne_out, div_out,
       divu_out, halt_out, j_out, jr_out, lw_out, Math_op_out, mfhi_out, mflo_out, mult_out, mulu_out,
       nop_out, nor_out, or_out, pop_push_out, slt_out, slti_out, sltu_out, Sub_out, sw_out, xor_out;

  and Math_op (Math_op_out, ~Instruction[26], ~Instruction[27], ~Instruction[28], ~Instruction[29], ~Instruction[30], ~Instruction[31]);  // AND_Gate
  and pop_push (pop_push_out, ~Instruction[26], ~Instruction[27], ~Instruction[28], Instruction[29], Instruction[30], Instruction[31]);  // AND_Gate
  and halt (halt_out, Instruction[26], Instruction[27], Instruction[28], Instruction[29], Instruction[30], Instruction[31]);
  and add (add_out, ~Instruction[0], ~Instruction[1], ~Instruction[2], ~Instruction[3], ~Instruction[4], Instruction[5]);  // AND_Gate
  and div (div_out, ~Instruction[0], Instruction[1], ~Instruction[2], Instruction[3], Instruction[4], ~Instruction[5]);  // AND_Gate
  and \nor  (nor_out, Instruction[0], Instruction[1], Instruction[2], ~Instruction[3], ~Instruction[4], Instruction[5]);  // AND_Gate
  and mfhi (mfhi_out, ~Instruction[0], ~Instruction[1], ~Instruction[2], ~Instruction[3], Instruction[4], ~Instruction[5]);  // AND_Gate
  and Sub (Sub_out, ~Instruction[0], Instruction[1], ~Instruction[2], ~Instruction[3], ~Instruction[4], Instruction[5]);  // AND_Gate
  and divu (divu_out, Instruction[0], Instruction[1], ~Instruction[2], Instruction[3], Instruction[4], ~Instruction[5]);  // AND_Gate
  and \xor  (xor_out, ~Instruction[0], ~Instruction[1], ~Instruction[2], Instruction[3], ~Instruction[4], Instruction[5]);  // AND_Gate
  and mflo (mflo_out, ~Instruction[0], Instruction[1], ~Instruction[2], ~Instruction[3], Instruction[4], ~Instruction[5]);  // AND_Gate
  and addi (addi_out, ~Instruction[26], ~Instruction[27], ~Instruction[28], Instruction[29], ~Instruction[30], ~Instruction[31]);  // AND_Gate
  and andi (andi_out, ~Instruction[26], ~Instruction[27], Instruction[28], Instruction[29], ~Instruction[30], ~Instruction[31]);  // AND_Gate
  and slti (slti_out, ~Instruction[26], Instruction[27], ~Instruction[28], Instruction[29], ~Instruction[30], ~Instruction[31]);  // AND_Gate
  and beq (beq_out, ~Instruction[26], ~Instruction[27], Instruction[28], ~Instruction[29], ~Instruction[30], ~Instruction[31]);  // AND_Gate
  and bne (bne_out, Instruction[26], ~Instruction[27], Instruction[28], ~Instruction[29], ~Instruction[30], ~Instruction[31]);  // AND_Gate
  and mult (mult_out, ~Instruction[0], ~Instruction[1], ~Instruction[2], Instruction[3], Instruction[4], ~Instruction[5]);  // AND_Gate
  and \and  (and_out, ~Instruction[0], ~Instruction[1], Instruction[2], ~Instruction[3], ~Instruction[4], Instruction[5]);  // AND_Gate
  and slt (slt_out, ~Instruction[0], Instruction[1], ~Instruction[2], Instruction[3], ~Instruction[4], Instruction[5]);  // AND_Gate
  and nop (nop_out, ~Instruction[0], ~Instruction[1], ~Instruction[2], ~Instruction[3], ~Instruction[4], ~Instruction[5]);  // AND_Gate
  and blez (blez_out, ~Instruction[26], Instruction[27], Instruction[28], ~Instruction[29], ~Instruction[30], ~Instruction[31]);  // AND_Gate
  and bgtz (bgtz_out, Instruction[26], Instruction[27], Instruction[28], ~Instruction[29], ~Instruction[30], ~Instruction[31]);  // AND_Gate
  and bltz (bltz_out, Instruction[26], ~Instruction[27], ~Instruction[28], ~Instruction[29], ~Instruction[30], ~Instruction[31]);  // AND_Gate
  and lw (lw_out, Instruction[26], Instruction[27], ~Instruction[28], ~Instruction[29], ~Instruction[30], Instruction[31]);  // AND_Gate
  and sw (sw_out, Instruction[26], Instruction[27], ~Instruction[28], Instruction[29], ~Instruction[30], Instruction[31]);  // AND_Gate
  and mulu (mulu_out, Instruction[0], ~Instruction[1], ~Instruction[2], Instruction[3], Instruction[4], ~Instruction[5]);  // AND_Gate
  and \or  (or_out, Instruction[0], ~Instruction[1], Instruction[2], ~Instruction[3], ~Instruction[4], Instruction[5]);  // AND_Gate
  and sltu (sltu_out, Instruction[0], Instruction[1], ~Instruction[2], Instruction[3], ~Instruction[4], Instruction[5]);  // AND_Gate
  and jr (jr_out, ~Instruction[0], ~Instruction[1], ~Instruction[2], Instruction[3], ~Instruction[4], ~Instruction[5]);  // AND_Gate
  and j (j_out, ~Instruction[26], Instruction[27], ~Instruction[28], ~Instruction[29], ~Instruction[30], ~Instruction[31]);  // AND_Gate

  assign out_2 = Instruction[25:0];
  assign out_3 = Instruction[15:11];
  assign out_4 = Instruction[20:16];
  assign out_5 = Instruction[25:21];
  assign out_6 = Instruction[15:0];

  // Other names for the same wires on the sheet: Constante[15:0] = Instruction[15:0];
  //   Destino_Salto[25:0] = Instruction[25:0]; Func_code[5:0] = Instruction[5:0]; x[4:0] = Instruction[10:6];
  //   Rd[4:0] = Instruction[15:11]; Rt[4:0] = Instruction[20:16]; Rs[4:0] = Instruction[25:21];
  //   Op_Code[5:0] = Instruction[31:26]

  // Notes on the sheet:
  //   Op-Code
  //   Tipo R
  //   Instruction Decoder
  //   Tipo I
  //   Func-Code
  //   Tipo J
  //   Outpout
endmodule
